// Logisim project leftshift32_template.circ as structural Verilog: 1 circuit, main circuit LeftShift32
module LeftShift32 (
  input  [31:0] B,
  input  [4:0] Sa,
  input  Cin,
  output [31:0] C
);


  // Notes on the sheet:
  //   ENTREES pour votre circuit
  //   NE PAS CHANGER LES ENTREES ET SORTIES DE VOTRE CIRCUIT !
  //   SORTIE pour votre circuit
endmodule
